# Fritzing sketch EsquemaMao1 (saved by Fritzing 0.9.3b)

parts:
  MyoWare_Sensor_Muscular = MyoWare Cable Shield
  Indicador = Dagu DGServo 9g (Top view) [part_number=RS001B]
  Modulo_LDR = LM393 LDR breakout [part_number=100027]
  Componente2 = Arduino Uno (Rev3)
  Polegar_Rotacao = Dagu DGServo 9g (Top view) [part_number=RS001B]
  Polegar_Flexao = Dagu DGServo 9g (Top view) [part_number=RS001B]
  Minimo = Dagu DGServo 9g (Top view) [part_number=RS001B]
  Anelar = Dagu DGServo 9g (Top view) [part_number=RS001B]
  Medio = Dagu DGServo 9g (Top view) [part_number=RS001B]
  Pulso_1 = Dagu DGServo 9g (Top view) [part_number=RS001B]
  Pulso_2 = Dagu DGServo 9g (Top view) [part_number=RS001B]
  Sensor_Shield_V5 = Arduino Sensor Shield v5.0
  VCC1 = Battery  # not connected

nets:
  VCC: MyoWare_Sensor_Muscular.VCC, Modulo_LDR.VCC, Componente2.A2, Polegar_Rotacao.vcc, Pulso_1.vcc, Pulso_2.vcc, Sensor_Shield_V5.+5V#94, Sensor_Shield_V5.+5V#105, Sensor_Shield_V5.+5V#106, Sensor_Shield_V5.+5V#107, Sensor_Shield_V5.+5V#108, Sensor_Shield_V5.+5V#109, Sensor_Shield_V5.+5V#112
  GND: MyoWare_Sensor_Muscular.GND, Modulo_LDR.GND, Componente2.A5/SCL, Componente2.RESET, Polegar_Rotacao.gnd, Polegar_Flexao.gnd, Pulso_1.gnd, Pulso_2.gnd, Sensor_Shield_V5.GND#62, Sensor_Shield_V5.GND#96, Sensor_Shield_V5.GND#113, Sensor_Shield_V5.GND#120, Sensor_Shield_V5.GND#121, Sensor_Shield_V5.GND#122, Sensor_Shield_V5.GND#123, Sensor_Shield_V5.GND#124
  N1: Indicador.gnd, Sensor_Shield_V5.GND#127
  VCC_2: Indicador.vcc, Polegar_Flexao.vcc, Sensor_Shield_V5.A5, Sensor_Shield_V5.+5V#55, Sensor_Shield_V5.+5V#89
  N2: Indicador.pulse, Sensor_Shield_V5.D5
  N3: Modulo_LDR.AO, Modulo_LDR.DO, Sensor_Shield_V5.D10#68
  VCC_3: Componente2.A3, Componente2.A4/SDA, Anelar.vcc, Medio.vcc, Sensor_Shield_V5.A0, Sensor_Shield_V5.A1, Sensor_Shield_V5.+5V#90, Sensor_Shield_V5.+5V#91
  N4: Componente2.ioref, Sensor_Shield_V5.+5V#51, Sensor_Shield_V5.3.3V
  N5: Componente2.3V3, Sensor_Shield_V5.D11
  5V: Componente2.5V, Minimo.vcc, Sensor_Shield_V5.D10#50, Sensor_Shield_V5.+5V#92
  N6: Componente2.GND, Sensor_Shield_V5.D12, Sensor_Shield_V5.D13
  N7: Polegar_Rotacao.pulse, Sensor_Shield_V5.D7
  N8: Polegar_Flexao.pulse, Sensor_Shield_V5.D6
  GND_2: Minimo.gnd, Anelar.gnd, Sensor_Shield_V5.GND#128, Sensor_Shield_V5.GND#129
  N9: Minimo.pulse, Sensor_Shield_V5.D2
  N10: Anelar.pulse, Sensor_Shield_V5.D3
  N11: Medio.gnd, Sensor_Shield_V5.GND#144
  N12: Medio.pulse, Sensor_Shield_V5.D4
  N13: Pulso_1.pulse, Sensor_Shield_V5.D8
  N14: Pulso_2.pulse, Sensor_Shield_V5.D9

custom parts:
  Battery: Your standard 2x 18650 battery pack (7,4 Volts)
