# Fritzing sketch Esquematico_TCC (saved by Fritzing 0.9.3b)

parts:
  MyoWare_Sensor_Muscular = MyoWare Cable Shield
  Indicador = Dagu DGServo 9g (Top view) [part_number=RS001B]
  Modulo_LDR = LM393 LDR breakout [part_number=100027]
  Polegar_Rotacao = Dagu DGServo 9g (Top view) [part_number=RS001B]
  Polegar_Flexao = Dagu DGServo 9g (Top view) [part_number=RS001B]
  Minimo = Dagu DGServo 9g (Top view) [part_number=RS001B]
  Anelar = Dagu DGServo 9g (Top view) [part_number=RS001B]
  Medio = Dagu DGServo 9g (Top view) [part_number=RS001B]
  Pulso_1 = Dagu DGServo 9g (Top view) [part_number=RS001B]
  Pulso_2 = Dagu DGServo 9g (Top view) [part_number=RS001B]
  Sensor_Shield_V5 = Arduino Sensor Shield v5.0
  VCC1 = Battery

nets:
  VCC: MyoWare_Sensor_Muscular.VCC, Indicador.vcc, Modulo_LDR.VCC, Polegar_Rotacao.vcc, Polegar_Flexao.vcc, Minimo.vcc, Anelar.vcc, Medio.vcc, Pulso_1.vcc, Pulso_2.vcc, Sensor_Shield_V5.+5V, VCC1.+
  GND: MyoWare_Sensor_Muscular.GND, Modulo_LDR.GND, Sensor_Shield_V5.GND
  GND_2: Indicador.gnd, Polegar_Rotacao.gnd, Polegar_Flexao.gnd, Minimo.gnd, Anelar.gnd, Medio.gnd, Pulso_1.gnd, Pulso_2.gnd
  N1: Indicador.pulse, Sensor_Shield_V5.D5
  N2: Modulo_LDR.DO, Sensor_Shield_V5.D10
  N3: Polegar_Rotacao.pulse, Sensor_Shield_V5.D7
  N4: Polegar_Flexao.pulse, Sensor_Shield_V5.D6
  N5: Minimo.pulse, Sensor_Shield_V5.D2
  N6: Anelar.pulse, Sensor_Shield_V5.D3
  N7: Medio.pulse, Sensor_Shield_V5.D4
  N8: Pulso_1.pulse, Sensor_Shield_V5.D9
  N9: Pulso_2.pulse, Sensor_Shield_V5.D8

notes:
  9,

custom parts:
  Battery: Your standard 2x 18650 battery pack (7,4 Volts)
